# Fritzing sketch DevreSemasi (saved by Fritzing 0.9.3b)
breadboards: 1

parts:
  Parça1 = Arduino Uno (Rev3) - ICSP
  hc-sr1 = hc-sr04
  LED1 = smd LED [color="Red (633nm)" package="0603 [SMD]"]
  LED2 = smd LED [color="Red (633nm)" package="0603 [SMD]"]
  LED3 = smd LED [color="Red (633nm)" package="0603 [SMD]"]
  Parça2 = Bluetooth HC-05 Macho
  R1 = Resistor [tolerance=±5% resistance=220 package="1206 [SMD]"]
  R2 = Resistor [tolerance=±5% resistance=220 package="1206 [SMD]"]
  M1 = DC Motor
  R3 = Resistor [tolerance=±5% resistance=220 package="1206 [SMD]"]

nets:
  N1: Parça1.ICSP_MISO, Parça1.D12/MISO, R2.Pin_1
  VCC: Parça1.5V, hc-sr1.VCC, Parça2.VCC
  N2: Parça1.D10_PWM/SS, R3.Pin_1
  N3: Parça1.D11_PWM/MOSI, M1.pin_1
  N4: Parça1.D13/SCK, R1.Pin_1
  GND: Parça1.GND, hc-sr1.GND, LED1.cathode, LED2.cathode, LED3.cathode, Parça2.GND, M1.pin_2
  N5: Parça1.D0/RX, Parça2.TXD
  N6: Parça1.D1/TX, Parça2.RXD
  N7: Parça1.D6_PWM, hc-sr1.Echo
  N8: Parça1.D7, hc-sr1.Trig
  N9: LED1.anode, R1.Pin_0
  N10: LED2.anode, R2.Pin_0
  N11: LED3.anode, R3.Pin_0
